// Logisim project Main bus.circ as structural Verilog: 1 circuit, main circuit Main bus
module Main_bus (
  input  in_1,
  input  in_2,
  input  in_3,
  input  in_4,
  input  in_5,
  input  in_6,
  input  in_7,
  input  in_8,
  input  in_9,
  input  in_10,
  input  in_11,
  input  [15:0] in_12
);

  wire [15:0] Accumulator_register_q, controlled_buffer_1_out, controlled_buffer_3_out,
       controlled_buffer_4_out, controlled_buffer_5_out, controlled_buffer_7_out, controlled_buffer_8_out,
       Input_register_2_q, Input_register_q, Instruction_register_q, Memory_access_register_q,
       Output_register_q, Program_counter_q, ram_1_data, rom_1_data, undriven;

  Counter #(.width(16), .max('hffff)) Program_counter (
    .count(in_3), .Q(Program_counter_q), .clk(in_4));  // open: load, D, carry, clr
  Register #(.width(16)) Memory_access_register (
    .D(controlled_buffer_3_out), .en(1'b1), .Q(Memory_access_register_q), .clk(in_4));  // open: clr
  Register #(.width(16)) Instruction_register (
    .D(controlled_buffer_8_out), .en(1'b1), .Q(Instruction_register_q), .clk(in_4));  // open: clr
  RAM #(.addrWidth(16), .dataWidth(16)) ram_1 (
    .addr(Memory_access_register_q), .data(ram_1_data), .clk(in_4), .ld(1'b1));  // open: sel, clr
  ROM #(.addrWidth(16), .dataWidth(16)) rom_1 (.addr(Instruction_register_q), .data(rom_1_data));  // open: sel
  assign controlled_buffer_1_out = in_2 ? Accumulator_register_q : 16'bz;  // Controlled_Buffer controlled_buffer_1
  assign controlled_buffer_1_out = in_1 ? Program_counter_q : 16'bz;  // Controlled_Buffer controlled_buffer_2
  assign controlled_buffer_3_out = in_5 ? controlled_buffer_1_out : 16'bz;  // Controlled_Buffer controlled_buffer_3
  assign controlled_buffer_4_out = in_6 ? controlled_buffer_1_out : 16'bz;  // Controlled_Buffer controlled_buffer_4
  assign controlled_buffer_5_out = in_8 ? controlled_buffer_1_out : 16'bz;  // Controlled_Buffer controlled_buffer_5
  assign controlled_buffer_1_out = in_7 ? ram_1_data : 16'bz;  // Controlled_Buffer controlled_buffer_6
  assign controlled_buffer_7_out = in_10 ? controlled_buffer_1_out : 16'bz;  // Controlled_Buffer controlled_buffer_7
  assign controlled_buffer_8_out = in_9 ? controlled_buffer_1_out : 16'bz;  // Controlled_Buffer controlled_buffer_8
  assign controlled_buffer_1_out = in_11 ? in_12 : 16'bz;  // Controlled_Buffer controlled_buffer_9
  Register #(.width(16)) Accumulator_register (
    .D(undriven), .en(1'b1), .Q(Accumulator_register_q), .clr(in_4));  // open: clk
  Register #(.width(16)) Input_register (
    .D(controlled_buffer_4_out), .en(1'b1), .Q(Input_register_q), .clk(in_4));  // open: clr
  Register #(.width(16)) Input_register_2 (
    .D(controlled_buffer_5_out), .en(1'b1), .Q(Input_register_2_q), .clk(in_4));  // open: clr
  Register #(.width(16)) Output_register (
    .D(controlled_buffer_7_out), .Q(Output_register_q), .clk(in_4));  // open: en, clr
  Hex_Digit_Display hex_digit_display_1 (.value(Output_register_q[15:12]));  // open: dp
  Hex_Digit_Display hex_digit_display_2 (.value(Output_register_q[7:4]));  // open: dp
  Hex_Digit_Display hex_digit_display_3 (.value(Output_register_q[11:8]));  // open: dp
  Hex_Digit_Display hex_digit_display_4 (.value(Output_register_q[3:0]));  // open: dp

  // Notes on the sheet:
  //   ROM for control matrix
  //   ALU
endmodule
